# Fritzing sketch Design1 (saved by Fritzing 0.9.6b)
perfboards: 1

parts:
  LED1 = LED - 5mm [color="Red (633nm)" current=0.030 package="5 mm [THT]"]
  LED2 = LED - 5mm [color="Red (633nm)" current=0.030 package="5 mm [THT]"]
  MCU1 = Raspberry Pi Zero
  LED3 = LED - 5mm [color="Red (633nm)" current=0.030 package="5 mm [THT]"]
  LED4 = LED - 5mm [color="Red (633nm)" current=0.030 package="5 mm [THT]"]  # not connected
  R2 = Resistor [tolerance=±5% power=0.25 resistance=220 package=THT]
  R3 = Resistor [tolerance=±5% power=0.25 resistance=220 package=THT]

nets:
  N1: LED1.cathode, R3.Pin_1
  N2: LED1.anode, LED2.cathode, MCU1.pin_10
  N3: LED3.cathode, R2.Pin_1
